# Fritzing sketch sensor-luz (saved by Fritzing 0.9.3b)
breadboards: 1

parts:
  R1 = Photocell (LDR) [package=THT]
  Raspberry_Pi_1 = Raspberry Pi 3 [part_number=RPI-3-V1.2]

nets:
  N1: R1.pin_0, Raspberry_Pi_1.GND
  N2: R1.pin_1, Raspberry_Pi_1.GPIO18
